// Logisim project ETFStudent.circ as structural Verilog: 10 circuits, main circuit ROM32x24
module ROM32x24 (
  input  [4:0] A4__0,
  input  CS,
  output [23:0] DOUT
);

  ROM #(.addrWidth(5), .dataWidth(24)) rom_1 (.addr(A4__0), .data(DOUT), .sel(CS));
endmodule

module DC5_32 (
  input  I0,
  input  I1,
  input  I2,
  input  I3,
  input  I4,
  input  EN,
  output out_7,
  output out_8,
  output out_9,
  output out_10,
  output out_11,
  output out_12,
  output out_13,
  output out_14,
  output out_15,
  output out_16,
  output out_17,
  output out_18,
  output out_19,
  output out_20,
  output out_21,
  output out_22,
  output out_23,
  output out_24,
  output out_25,
  output out_26,
  output out_27,
  output out_28,
  output out_29,
  output out_30,
  output out_31,
  output out_32,
  output out_33,
  output out_34,
  output out_35,
  output out_36,
  output out_37,
  output out_38
);

  wire dc2_4_1_p3, dc2_4_1_p4, dc2_4_1_p5, dc2_4_1_p6;

  // DC2_4 dc2_4_1: pin names not known; wires that end beside it: {I4, I3}, EN, dc2_4_1_p3, dc2_4_1_p4, dc2_4_1_p5, dc2_4_1_p6
  // DC3_8 dc3_8_1: pin names not known; wires that end beside it: {I2, I1, I0}, dc2_4_1_p3, out_7, out_8, out_9, out_10, out_11, out_12, out_13, out_14
  // DC3_8 dc3_8_2: pin names not known; wires that end beside it: {I2, I1, I0}, dc2_4_1_p4, out_15, out_16, out_17, out_18, out_19, out_20, out_21, out_22
  // DC3_8 dc3_8_3: pin names not known; wires that end beside it: {I2, I1, I0}, dc2_4_1_p5, out_23, out_24, out_25, out_26, out_27, out_28, out_29, out_30
  // DC3_8 dc3_8_4: pin names not known; wires that end beside it: {I2, I1, I0}, dc2_4_1_p6, out_31, out_32, out_33, out_34, out_35, out_36, out_37, out_38
endmodule

module REG16_DEC_LD (
  input  [15:0] in_1,
  input  in_2,
  input  in_3,
  input  in_4,
  output [15:0] out_5
);

  // REG16 reg16_1: pin names not known; wires that end beside it: in_4, in_1, out_5, in_2, in_3
endmodule

module GPR16x16 (
  input  [15:0] DI15__0,
  input  [3:0] A3__0,
  input  WR,
  input  CLK,
  output [15:0] DO15__0
);

  wire and_9_out, and_10_out, and_11_out, and_13_out, and_15_out, and_16_out, CS0, CS1, CS2, CS3, CS4, CS5,
       CS6, CS7, CS8, CS9, CS10, CS11, CS12, CS13, CS14, CS15, reg16_ld_1_p4, reg16_ld_2_p4, reg16_ld_3_p4,
       reg16_ld_4_p4, reg16_ld_5_p4, reg16_ld_6_p4, reg16_ld_7_p4, reg16_ld_8_p4, reg16_ld_12_p4,
       reg16_ld_14_p4;
  wire [15:0] reg16_ld_1_p3, reg16_ld_2_p3, reg16_ld_3_p3, reg16_ld_4_p3, reg16_ld_5_p3, reg16_ld_6_p3,
       reg16_ld_7_p3, reg16_ld_8_p3, reg16_ld_9_p3, reg16_ld_10_p3, reg16_ld_11_p3, reg16_ld_12_p3,
       reg16_ld_13_p3, reg16_ld_14_p3, reg16_ld_15_p3, reg16_ld_16_p3;

  // DC4_16 dc4_16_1: pin names not known; wires that end beside it: A3__0, 1'b1, CS0, CS1, CS2, CS3, CS4, CS5, CS6, CS7, CS8, CS9, CS10, CS11, CS12, CS13, CS14, CS15
  // REG16_LD reg16_ld_1: pin names not known; wires that end beside it: CLK, DI15__0, reg16_ld_1_p3, reg16_ld_1_p4
  assign DO15__0 = CS0 ? reg16_ld_1_p3 : 16'bz;  // Controlled_Buffer controlled_buffer_1
  // REG16_LD reg16_ld_2: pin names not known; wires that end beside it: CLK, DI15__0, reg16_ld_2_p3, reg16_ld_2_p4
  assign DO15__0 = CS1 ? reg16_ld_2_p3 : 16'bz;  // Controlled_Buffer controlled_buffer_2
  // REG16_LD reg16_ld_3: pin names not known; wires that end beside it: CLK, DI15__0, reg16_ld_3_p3, reg16_ld_3_p4
  assign DO15__0 = CS2 ? reg16_ld_3_p3 : 16'bz;  // Controlled_Buffer controlled_buffer_3
  // REG16_LD reg16_ld_4: pin names not known; wires that end beside it: CLK, DI15__0, reg16_ld_4_p3, reg16_ld_4_p4
  assign DO15__0 = CS3 ? reg16_ld_4_p3 : 16'bz;  // Controlled_Buffer controlled_buffer_4
  // REG16_LD reg16_ld_5: pin names not known; wires that end beside it: CLK, DI15__0, reg16_ld_5_p3, reg16_ld_5_p4
  assign DO15__0 = CS8 ? reg16_ld_5_p3 : 16'bz;  // Controlled_Buffer controlled_buffer_5
  // REG16_LD reg16_ld_6: pin names not known; wires that end beside it: CLK, DI15__0, reg16_ld_6_p3, reg16_ld_6_p4
  assign DO15__0 = CS9 ? reg16_ld_6_p3 : 16'bz;  // Controlled_Buffer controlled_buffer_6
  // REG16_LD reg16_ld_7: pin names not known; wires that end beside it: CLK, DI15__0, reg16_ld_7_p3, reg16_ld_7_p4
  assign DO15__0 = CS10 ? reg16_ld_7_p3 : 16'bz;  // Controlled_Buffer controlled_buffer_7
  // REG16_LD reg16_ld_8: pin names not known; wires that end beside it: CLK, DI15__0, reg16_ld_8_p3, reg16_ld_8_p4
  assign DO15__0 = CS11 ? reg16_ld_8_p3 : 16'bz;  // Controlled_Buffer controlled_buffer_8
  and and_1 (reg16_ld_1_p4, CS0, WR);
  and and_2 (reg16_ld_2_p4, CS1, WR);
  and and_3 (reg16_ld_3_p4, CS2, WR);
  and and_4 (reg16_ld_4_p4, CS3, WR);
  and and_5 (reg16_ld_5_p4, CS8, WR);
  and and_6 (reg16_ld_6_p4, CS9, WR);
  and and_7 (reg16_ld_7_p4, CS10, WR);
  and and_8 (reg16_ld_8_p4, CS11, WR);
  and and_9 (and_9_out, CS4, WR);
  // REG16_LD reg16_ld_9: pin names not known; wires that end beside it: CLK, DI15__0, reg16_ld_9_p3, and_9_out
  assign DO15__0 = CS4 ? reg16_ld_9_p3 : 16'bz;  // Controlled_Buffer controlled_buffer_9
  and and_10 (and_10_out, CS5, WR);
  // REG16_LD reg16_ld_10: pin names not known; wires that end beside it: CLK, DI15__0, reg16_ld_10_p3, and_10_out
  assign DO15__0 = CS5 ? reg16_ld_10_p3 : 16'bz;  // Controlled_Buffer controlled_buffer_10
  and and_11 (and_11_out, CS6, WR);
  // REG16_LD reg16_ld_11: pin names not known; wires that end beside it: CLK, DI15__0, reg16_ld_11_p3, and_11_out
  assign DO15__0 = CS6 ? reg16_ld_11_p3 : 16'bz;  // Controlled_Buffer controlled_buffer_11
  // REG16_LD reg16_ld_12: pin names not known; wires that end beside it: CLK, DI15__0, reg16_ld_12_p3, reg16_ld_12_p4
  and and_12 (reg16_ld_12_p4, CS7, WR);
  assign DO15__0 = CS7 ? reg16_ld_12_p3 : 16'bz;  // Controlled_Buffer controlled_buffer_12
  and and_13 (and_13_out, CS12, WR);
  // REG16_LD reg16_ld_13: pin names not known; wires that end beside it: CLK, DI15__0, reg16_ld_13_p3, and_13_out
  assign DO15__0 = CS12 ? reg16_ld_13_p3 : 16'bz;  // Controlled_Buffer controlled_buffer_13
  // REG16_LD reg16_ld_14: pin names not known; wires that end beside it: CLK, DI15__0, reg16_ld_14_p3, reg16_ld_14_p4
  and and_14 (reg16_ld_14_p4, CS13, WR);
  assign DO15__0 = CS13 ? reg16_ld_14_p3 : 16'bz;  // Controlled_Buffer controlled_buffer_14
  and and_15 (and_15_out, CS14, WR);
  // REG16_LD reg16_ld_15: pin names not known; wires that end beside it: CLK, DI15__0, reg16_ld_15_p3, and_15_out
  assign DO15__0 = CS14 ? reg16_ld_15_p3 : 16'bz;  // Controlled_Buffer controlled_buffer_15
  and and_16 (and_16_out, CS15, WR);
  // REG16_LD reg16_ld_16: pin names not known; wires that end beside it: CLK, DI15__0, reg16_ld_16_p3, and_16_out
  assign DO15__0 = CS15 ? reg16_ld_16_p3 : 16'bz;  // Controlled_Buffer controlled_buffer_16

  // Other names for the same wires on the sheet: inREG[15:0] = DI15__0; outREG[15:0] = DO15__0
endmodule

module KMADR (
  input  immed,
  input  memind,
  input  regind,
  input  regdir,
  input  predec,
  input  pcrelpom,
  output [3:0] out_7
);

  assign out_7 = memind ? 4'b0011 : 4'bz;  // Controlled_Buffer controlled_buffer_1
  assign out_7 = immed ? 4'b0010 : 4'bz;  // Controlled_Buffer controlled_buffer_2
  assign out_7 = regind ? 4'b1001 : 4'bz;  // Controlled_Buffer controlled_buffer_3
  assign out_7 = regdir ? 4'b1010 : 4'bz;  // Controlled_Buffer controlled_buffer_4
  assign out_7 = predec ? 4'b1011 : 4'bz;  // Controlled_Buffer controlled_buffer_5
  assign out_7 = pcrelpom ? 4'b1110 : 4'bz;  // Controlled_Buffer controlled_buffer_6
endmodule

module ROM32x24_2 (
  input  [4:0] A4__0,
  input  CS,
  output [23:0] DOUT
);

  ROM #(.addrWidth(5), .dataWidth(24)) rom_1 (.addr(A4__0), .data(DOUT), .sel(CS));
endmodule

module ALU16_SUB_XOR_AND (
  input  Cin,
  input  [15:0] A,
  input  [15:0] B,
  input  sub,
  input  \xor ,
  input  \and ,
  output [15:0] F,
  output Cout
);

  wire subtractor_1_bout;
  wire [15:0] and_1_out, subtractor_1_out, xor_1_out;

  Subtractor #(.width(16)) subtractor_1 (.a(A), .b(B), .out(subtractor_1_out), .bin(Cin), .bout(subtractor_1_bout));
  assign F = sub ? subtractor_1_out : 16'bz;  // Controlled_Buffer controlled_buffer_1
  assign Cout = sub ? subtractor_1_bout : 1'bz;  // Controlled_Buffer controlled_buffer_2
  assign xor_1_out = A ^ B;  // XOR_Gate xor_1, 16 bits wide
  assign and_1_out = A & B;  // AND_Gate and_1, 16 bits wide
  assign F = \xor  ? xor_1_out : 16'bz;  // Controlled_Buffer controlled_buffer_3
  assign F = \and  ? and_1_out : 16'bz;  // Controlled_Buffer controlled_buffer_4
endmodule

module ROM128x56 (
  input  [6:0] A6__0,
  input  CS,
  output [23:0] DOUT,
  output [31:0] DOUT_2
);

  ROM #(.addrWidth(7), .dataWidth(32)) rom_1 (.addr(A6__0), .data(DOUT_2), .sel(CS));
  ROM #(.addrWidth(7), .dataWidth(24)) rom_2 (.addr(A6__0), .data(DOUT), .sel(CS));
endmodule

module KMADR_EXEC (
  input  LD,
  input  ST,
  input  DEC,
  input  SUB,
  input  XOR,
  input  AND,
  input  STRFIND,
  input  BOVF,
  input  BNCR,
  input  BLEQ,
  input  BLSSU,
  input  JLEQ,
  input  JMP,
  input  JSR,
  input  RTS,
  input  RTI,
  input  ROR,
  input  PUSH,
  input  POP,
  input  HALT,
  output [6:0] out_21
);

  assign out_21 = ST ? 7'b0000100 : 7'bz;  // Controlled_Buffer controlled_buffer_1
  assign out_21 = LD ? 7'b0000010 : 7'bz;  // Controlled_Buffer controlled_buffer_2
  assign out_21 = DEC ? 7'b0001011 : 7'bz;  // Controlled_Buffer controlled_buffer_3
  assign out_21 = XOR ? 7'b0010110 : 7'bz;  // Controlled_Buffer controlled_buffer_4
  assign out_21 = SUB ? 7'b0010100 : 7'bz;  // Controlled_Buffer controlled_buffer_5
  assign out_21 = AND ? 7'b0011000 : 7'bz;  // Controlled_Buffer controlled_buffer_6
  assign out_21 = STRFIND ? 7'b0011010 : 7'bz;  // Controlled_Buffer controlled_buffer_7
  assign out_21 = BOVF ? 7'b0100000 : 7'bz;  // Controlled_Buffer controlled_buffer_8
  assign out_21 = BNCR ? 7'b0100000 : 7'bz;  // Controlled_Buffer controlled_buffer_9
  assign out_21 = BLSSU ? 7'b0100000 : 7'bz;  // Controlled_Buffer controlled_buffer_10
  assign out_21 = BLEQ ? 7'b0100000 : 7'bz;  // Controlled_Buffer controlled_buffer_11
  assign out_21 = JLEQ ? 7'b0100010 : 7'bz;  // Controlled_Buffer controlled_buffer_12
  assign out_21 = JMP ? 7'b0100011 : 7'bz;  // Controlled_Buffer controlled_buffer_13
  assign out_21 = RTS ? 7'b0101010 : 7'bz;  // Controlled_Buffer controlled_buffer_14
  assign out_21 = JSR ? 7'b0100100 : 7'bz;  // Controlled_Buffer controlled_buffer_15
  assign out_21 = RTI ? 7'b1000011 : 7'bz;  // Controlled_Buffer controlled_buffer_16
  assign out_21 = PUSH ? 7'b0110101 : 7'bz;  // Controlled_Buffer controlled_buffer_17
  assign out_21 = ROR ? 7'b0110011 : 7'bz;  // Controlled_Buffer controlled_buffer_18
  assign out_21 = HALT ? 7'b1000001 : 7'bz;  // Controlled_Buffer controlled_buffer_19
  assign out_21 = POP ? 7'b0111011 : 7'bz;  // Controlled_Buffer controlled_buffer_20
endmodule

module ROM32x32 (
  input  [4:0] A4__0,
  input  CS,
  output [31:0] DOUT
);

  ROM #(.addrWidth(5), .dataWidth(32)) rom_1 (.addr(A4__0), .data(DOUT), .sel(CS));
endmodule
