// Logisim project ORT2Project.circ as structural Verilog: 8 circuits, main circuit COMPUTER
module COMPUTER (
);

  wire BTN_RST_out, CLK, cpu_1_inta, interrupt_interface_8_1_p4, interrupt_interface_8_1_p5,
       interrupt_interface_8_1_p6, interrupt_interface_8_1_p7, interrupt_interface_8_1_p8,
       interrupt_interface_8_1_p9, interrupt_interface_8_1_p10, interrupt_interface_8_1_p11,
       pull_resistor_3_node, pull_resistor_5_node, ram_1_out_8, rst;
  wire [2:0] cpu_1_uext2__0;
  wire [7:0] interrupt_interface_8_1_p1, pull_resistor_1_node, ram_1_out_7;
  wire [15:0] pull_resistor_4_node;

  Button BTN_RST (.out(BTN_RST_out));
  Clock u_CLK (.out(CLK));
  // RisingEdge risingedge_1: pin names not known; wires that end beside it: BTN_RST_out, CLK, rst
  RAM ram_1 (
    .in_1(pull_resistor_4_node), .in_2(CLK), .in_3(pull_resistor_1_node), .in_4(pull_resistor_3_node),
    .in_5(pull_resistor_5_node), .in_6(rst), .out_7(ram_1_out_7), .out_8(ram_1_out_8));
  Pull_Resistor pull_resistor_1 (.node(pull_resistor_1_node));
  Pull_Resistor pull_resistor_2 (.node(ram_1_out_7));
  Pull_Resistor pull_resistor_3 (.node(pull_resistor_3_node));
  Pull_Resistor pull_resistor_4 (.node(pull_resistor_4_node));
  Pull_Resistor pull_resistor_5 (.node(pull_resistor_5_node));
  Pull_Resistor pull_resistor_6 (.node(ram_1_out_8));
  CPU cpu_1 (
    .in_1(rst), .in_2(CLK), .in_3(ram_1_out_8), .in_4(ram_1_out_7), .ABUS(pull_resistor_4_node),
    .DOUTBUS(pull_resistor_1_node), .out_8(pull_resistor_3_node), .out_9(pull_resistor_5_node),
    .inta(cpu_1_inta), .intr7__0(interrupt_interface_8_1_p1), .UEXT2__0(cpu_1_uext2__0));
  // INTERRUPT_INTERFACE_8 interrupt_interface_8_1: pin names not known; wires that end beside it: interrupt_interface_8_1_p1, cpu_1_inta, cpu_1_uext2__0, interrupt_interface_8_1_p4, interrupt_interface_8_1_p5, interrupt_interface_8_1_p6, interrupt_interface_8_1_p7, interrupt_interface_8_1_p8, interrupt_interface_8_1_p9, interrupt_interface_8_1_p10, interrupt_interface_8_1_p11, CLK
  Button BTN_INTR7 (.out(interrupt_interface_8_1_p4));
  Button BTN_INTR6 (.out(interrupt_interface_8_1_p5));
  Button BTN_INTR5 (.out(interrupt_interface_8_1_p6));
  Button BTN_INTR4 (.out(interrupt_interface_8_1_p7));
  Button BTN_INTR3 (.out(interrupt_interface_8_1_p8));
  Button BTN_INTR2 (.out(interrupt_interface_8_1_p9));
  Button BTN_INTR1 (.out(interrupt_interface_8_1_p10));
  Button BTN_INTR0 (.out(interrupt_interface_8_1_p11));
endmodule

module CPU (
  input  in_1,
  input  in_2,
  input  in_3,
  input  [7:0] in_4,
  input  [7:0] intr7__0,
  output [15:0] ABUS,
  output [7:0] DOUTBUS,
  output out_8,
  output out_9,
  output inta,
  output [2:0] UEXT2__0
);

  wire [3:0] common_1_phaseffbus;
  wire [5:0] common_1_addrbus, pull_resistor_2_node;
  wire [7:0] pull_resistor_7_node;
  wire [14:0] pull_resistor_5_node;
  wire [15:0] A, ALU, B, INTRADDR, PSW;
  wire [19:0] common_1_instrucbus;
  wire [31:0] pull_resistor_6_node;

  COMMON common_1 (
    .CLK(in_2), .RST(in_1), .DIN(in_4), .CMEMBUS(pull_resistor_6_node), .MAR(ABUS), .MDR(DOUTBUS),
    .PHASEFFBUS(common_1_phaseffbus), .INSTRUCBUS(common_1_instrucbus), .ADDRBUS(common_1_addrbus),
    .PSW(PSW), .CREGBUS(pull_resistor_5_node), .CFFBUS(pull_resistor_7_node), .B(B), .A(A),
    .CPSW(pull_resistor_2_node), .ALU(ALU), .IVTPPDSP(INTRADDR));
  Pull_Resistor pull_resistor_1 (.node(common_1_phaseffbus));
  Pull_Resistor pull_resistor_2 (.node(pull_resistor_2_node));
  Pull_Resistor pull_resistor_3 (.node(common_1_instrucbus));
  Pull_Resistor pull_resistor_4 (.node(common_1_addrbus));
  Pull_Resistor pull_resistor_5 (.node(pull_resistor_5_node));
  Pull_Resistor pull_resistor_6 (.node(pull_resistor_6_node));
  Pull_Resistor pull_resistor_7 (.node(pull_resistor_7_node));
  FETCH fetch_1 (
    .in_1(in_1), .in_2(in_2), .in_3(in_3), .PHASEFFBUS(common_1_phaseffbus),
    .INSTRUCBUS(common_1_instrucbus), .ADDRBUS(common_1_addrbus), .PSW(PSW), .rdMEM(out_9),
    .CMEMBUS(pull_resistor_6_node), .CFFBUS(pull_resistor_7_node), .CREGBUS(pull_resistor_5_node));
  ADDR addr_1 (
    .in_1(in_1), .in_2(in_2), .in_3(in_3), .PHASEFFBUS(common_1_phaseffbus),
    .INSTRUCBUS(common_1_instrucbus), .ADDRBUS(common_1_addrbus), .rdMEM(out_9),
    .CMEMBUS(pull_resistor_6_node), .CFFBUS(pull_resistor_7_node), .CREGBUS(pull_resistor_5_node));
  EXEC exec_1 (
    .in_1(in_1), .in_2(in_2), .in_3(in_3), .B(B), .PHASEFFBUS(common_1_phaseffbus),
    .INSTRUCBUS(common_1_instrucbus), .ADDRBUS(common_1_addrbus), .PSW(PSW), .A(A), .ALU(ALU),
    .CMEMBUS(pull_resistor_6_node), .CFFBUS(pull_resistor_7_node), .CREGBUS(pull_resistor_5_node),
    .CPSW(pull_resistor_2_node), .rdMEM(out_9), .wrMEM(out_8), .in_9(DOUTBUS));
  INTR intr_1 (
    .in_1(in_1), .in_2(in_2), .in_3(in_3), .PHASEFFBUS(common_1_phaseffbus),
    .INSTRUCBUS(common_1_instrucbus), .PSW(PSW), .intr(intr7__0), .ADDIVTP(INTRADDR),
    .CMEMBUS(pull_resistor_6_node), .CFFBUS(pull_resistor_7_node), .CREGBUS(pull_resistor_5_node),
    .rdMEM(out_9), .wrMEM(out_8), .UEXT2__0(UEXT2__0), .inta(inta));

  // Other names for the same wires on the sheet: CLK = in_2; DIN7__0[7:0] = in_4; FCBUS = in_3; MAR[15:0] = ABUS;
  //   MDR[7:0] = DOUTBUS; RD = out_9; rst = in_1; WR = out_8
endmodule

module COMMON (
  input  CLK,
  input  RST,
  input  [7:0] DIN,
  input  [15:0] A,
  input  [15:0] ALU,
  input  [15:0] IVTPPDSP,
  input  [31:0] CMEMBUS,
  input  [7:0] CFFBUS,
  input  [14:0] CREGBUS,
  input  [5:0] CPSW,
  output [15:0] MAR,
  output [7:0] MDR,
  output [3:0] PHASEFFBUS,
  output [19:0] INSTRUCBUS,
  output [5:0] ADDRBUS,
  output [15:0] PSW,
  output [15:0] B
);

  wire adrinst, and_1_out, and_2_out, and_3_out, and_4_out, and_5_out, and_6_out, and_7_out, and_8_out,
       and_9_out, and_10_out, and_11_out, and_12_out, and_13_out, and_14_out, and_15_out, and_16_out,
       and_17_out, and_18_out, and_19_out, and_20_out, and_21_out, and_22_out, and_23_out, and_24_out,
       bezadrinst, branchinst, jmpinst, mp4_8b_1_p5, mp4_8b_2_p5, mp8_8b_1_p7, mp8_16b_1_p8, mp8_16b_2_p7,
       not_1_out, not_6_out, or_1_out, or_3_out, or_4_out, or_5_out, or_6_out, or_7_out, or_8_out, or_9_out,
       or_10_out, reg16_inc_ld_1_p5, rsff_2_p4, rsff_3_p4, rsff_4_p4, rsff_5_p4, rsff_7_p4, rsff_8_p4,
       rsff_9_p4, rsff_10_p4;
  wire [3:0] IR27__24;
  wire [6:5] PSW8b;
  wire [7:0] Bdec7__0, Bdec15__8, GPR7__0, IR7__0, IR15__8, IR23__16, PC7__0;
  wire [7:4] IR31__24;
  wire [15:0] ADDbranch, ADDIVTP15__0, ADDrelp, DW, inPC, mp2_16b_1_p3, mp2_16b_2_p3, SP15__0;
  wire [15:8] GPR15__0, PC15__0;

  // REG8_LD reg8_ld_1: pin names not known; wires that end beside it: CLK, MDR, {IR31__24, IR27__24}, CREGBUS[0]
  // REG8_LD reg8_ld_2: pin names not known; wires that end beside it: CLK, MDR, IR23__16, CREGBUS[1]
  // MP4_8b mp4_8b_1: pin names not known; wires that end beside it: CREGBUS[7], CREGBUS[6], MDR, IR15__8, mp4_8b_1_p5, GPR15__0, Bdec15__8, 1'b1
  // REG8_LD reg8_ld_3: pin names not known; wires that end beside it: CLK, mp4_8b_1_p5, B[15:8], CREGBUS[4]
  // REG8_LD reg8_ld_4: pin names not known; wires that end beside it: CLK, MDR, DW[15:8], CREGBUS[14]
  // MP8_16b mp8_16b_1: pin names not known; wires that end beside it: CMEMBUS[7], CMEMBUS[6], CMEMBUS[5], {PC15__0, PC7__0}, {IR15__8, IR7__0}, B, {GPR15__0, GPR7__0}, mp8_16b_1_p8, mp8_16b_1_p8, ADDrelp, SP15__0, ADDIVTP15__0, 1'b1
  // REG16 reg16_1: pin names not known; wires that end beside it: CLK, MAR, CMEMBUS[0], CMEMBUS[1], CMEMBUS[11]
  // DC4_16 dc4_16_1: pin names not known; wires that end beside it: IR31__24, PSW[0], bezadrinst, branchinst, jmpinst, adrinst
  // DC4_16 dc4_16_2: pin names not known; wires that end beside it: IR27__24, branchinst, INSTRUCBUS[6], INSTRUCBUS[7], INSTRUCBUS[8], INSTRUCBUS[9], INSTRUCBUS[10]
  // MP2_16b mp2_16b_1: pin names not known; wires that end beside it: CREGBUS[12], B, mp2_16b_1_p3, A, 1'b1
  GPR16x16 gpr16x16_1 (
    .DI15__0(mp2_16b_1_p3), .A3__0(IR23__16[3:0]), .WR(CREGBUS[8]), .CLK(CLK), .DO15__0({GPR15__0, GPR7__0}));
  // REG8_LD reg8_ld_5: pin names not known; wires that end beside it: CLK, MDR, IR15__8, CREGBUS[2]
  // MP4_8b mp4_8b_2: pin names not known; wires that end beside it: CREGBUS[7], CREGBUS[6], MDR, IR7__0, mp4_8b_2_p5, GPR7__0, Bdec7__0, 1'b1
  // REG8_LD reg8_ld_6: pin names not known; wires that end beside it: CLK, mp4_8b_2_p5, B[7:0], CREGBUS[5]
  // REG8_LD reg8_ld_7: pin names not known; wires that end beside it: CLK, MDR, DW[7:0], CREGBUS[13]
  // MP8_8b mp8_8b_1: pin names not known; wires that end beside it: CMEMBUS[8], CMEMBUS[9], DIN, A[15:8], A[7:0], PC15__0, mp8_8b_1_p7, PC7__0, B[15:8], B[7:0], {PSW[15], PSW8b, PSW[4:0]}, 1'b1
  // REG8_LD reg8_ld_8: pin names not known; wires that end beside it: CMEMBUS[10], CLK, mp8_8b_1_p7, MDR, CMEMBUS[2]
  // REG8_LD reg8_ld_9: pin names not known; wires that end beside it: CLK, MDR, IR7__0, CREGBUS[3]
  // DC4_16 dc4_16_3: pin names not known; wires that end beside it: IR27__24, bezadrinst, INSTRUCBUS[0], INSTRUCBUS[1], INSTRUCBUS[2], INSTRUCBUS[3], INSTRUCBUS[4], INSTRUCBUS[5]
  // DC4_16 dc4_16_4: pin names not known; wires that end beside it: IR27__24, jmpinst, INSTRUCBUS[11], INSTRUCBUS[12]
  // MP2_16b mp2_16b_2: pin names not known; wires that end beside it: CREGBUS[9], 16'h2, mp2_16b_2_p3, 16'h1, 1'b1
  Subtractor #(.width(16)) subtractor_1 (.a(B), .b(mp2_16b_2_p3), .out({Bdec15__8, Bdec7__0}));  // open: bin, bout
  or or_1 (or_1_out, CMEMBUS[14], RST);
  // REG16 reg16_2: pin names not known; wires that end beside it: CLK, 16'hf000, SP15__0, RST, CREGBUS[10], CREGBUS[11]
  not not_1 (not_1_out, RST);
  // RSFF rsff_1: pin names not known; wires that end beside it: CFFBUS[1], CLK, CFFBUS[0], not_1_out, PHASEFFBUS[0]
  // MP8_16b mp8_16b_2: pin names not known; wires that end beside it: CMEMBUS[12], CMEMBUS[13], inPC, 16'h1000, {IR23__16, IR15__8}, DW, mp8_16b_2_p7, ADDbranch, 1'b1
  // REG16_INC_LD reg16_inc_ld_1: pin names not known; wires that end beside it: or_1_out, CLK, mp8_16b_2_p7, {PC15__0, PC7__0}, reg16_inc_ld_1_p5, CMEMBUS[4]
  // DC4_16 dc4_16_5: pin names not known; wires that end beside it: IR27__24, adrinst, INSTRUCBUS[13], INSTRUCBUS[14], INSTRUCBUS[15], INSTRUCBUS[16], INSTRUCBUS[17], INSTRUCBUS[18], INSTRUCBUS[19]
  // DC4_16 dc4_16_6: pin names not known; wires that end beside it: IR23__16[7:4], adrinst, ADDRBUS[0], ADDRBUS[1], ADDRBUS[2], ADDRBUS[3], ADDRBUS[4], ADDRBUS[5]
  or or_2 (reg16_inc_ld_1_p5, CMEMBUS[3], RST);
  // ADD16 add16_1: pin names not known; wires that end beside it: {PC15__0, PC7__0}, ADDrelp, {{9{IR15__8[7]}}, IR15__8[6:0]}
  // RSFF rsff_2: pin names not known; wires that end beside it: CFFBUS[3], CLK, CFFBUS[2], rsff_2_p4, PHASEFFBUS[1]
  not not_2 (rsff_2_p4, RST);
  // ADD16 add16_2: pin names not known; wires that end beside it: {PC15__0, PC7__0}, ADDbranch, {{9{IR23__16[7]}}, IR23__16[6:0]}
  // RSFF rsff_3: pin names not known; wires that end beside it: CFFBUS[5], CLK, CFFBUS[4], rsff_3_p4, PHASEFFBUS[2]
  not not_3 (rsff_3_p4, RST);
  and and_1 (and_1_out, MDR[4], INSTRUCBUS[2]);
  and and_2 (and_2_out, CMEMBUS[21], INSTRUCBUS[16]);
  or or_3 (or_3_out, INSTRUCBUS[13], INSTRUCBUS[5], INSTRUCBUS[16], INSTRUCBUS[17], INSTRUCBUS[18], INSTRUCBUS[19]);
  or or_4 (or_4_out, INSTRUCBUS[13], INSTRUCBUS[5], INSTRUCBUS[16], INSTRUCBUS[3], INSTRUCBUS[17], INSTRUCBUS[18], INSTRUCBUS[19]);
  or or_5 (or_5_out, and_1_out, and_2_out);
  and and_3 (and_3_out, ~A[0], ~A[1], ~A[2], ~A[3], ~A[4], ~A[5], ~A[6], ~A[7], ~A[9], ~A[10], ~A[11], ~A[12], ~A[13], ~A[14], ~A[15], ~A[8]);  // AND_Gate
  // RSFF rsff_4: pin names not known; wires that end beside it: CFFBUS[7], CLK, CFFBUS[6], rsff_4_p4, PHASEFFBUS[3]
  not not_4 (rsff_4_p4, RST);
  and and_4 (and_4_out, MDR[1], INSTRUCBUS[2]);
  and and_5 (and_5_out, or_3_out, and_3_out);
  and and_6 (and_6_out, MDR[2], INSTRUCBUS[2]);
  and and_7 (and_7_out, or_4_out, A[15]);
  and and_8 (and_8_out, ~ALU[15], ~B[15], A[15]);  // AND_Gate
  and and_9 (and_9_out, ALU[15], B[15], ~A[15]);  // AND_Gate
  and and_10 (and_10_out, or_5_out, CMEMBUS[19]);
  or or_6 (or_6_out, and_4_out, and_5_out);
  or or_7 (or_7_out, and_6_out, and_7_out);
  and and_11 (and_11_out, INSTRUCBUS[16], or_8_out);
  or or_8 (or_8_out, and_8_out, and_9_out);
  and and_12 (and_12_out, ~or_5_out, CMEMBUS[19]);  // AND_Gate
  // RSFF rsff_5: pin names not known; wires that end beside it: and_12_out, CLK, and_10_out, rsff_5_p4, PSW[4]
  not not_5 (rsff_5_p4, RST);
  and and_13 (and_13_out, ~MDR[1], INSTRUCBUS[2], CMEMBUS[15]);  // AND_Gate
  and and_14 (and_14_out, MDR[1], INSTRUCBUS[2], CMEMBUS[15]);
  and and_15 (and_15_out, MDR[3], INSTRUCBUS[2]);
  or or_9 (or_9_out, and_15_out, and_11_out);
  or or_10 (or_10_out, and_13_out, CPSW[0]);
  and and_16 (and_16_out, ~or_6_out, CMEMBUS[16]);  // AND_Gate
  and and_17 (and_17_out, or_6_out, CMEMBUS[16]);
  and and_18 (and_18_out, ~or_7_out, CMEMBUS[17]);  // AND_Gate
  and and_19 (and_19_out, or_7_out, CMEMBUS[17]);
  not not_6 (not_6_out, RST);
  // RSFF rsff_6: pin names not known; wires that end beside it: or_10_out, CLK, and_14_out, not_6_out, PSW[0]
  // RSFF rsff_7: pin names not known; wires that end beside it: and_16_out, CLK, and_17_out, rsff_7_p4, PSW[1]
  not not_7 (rsff_7_p4, RST);
  // RSFF rsff_8: pin names not known; wires that end beside it: and_18_out, CLK, and_19_out, rsff_8_p4, PSW[2]
  not not_8 (rsff_8_p4, RST);
  and and_20 (and_20_out, ~or_9_out, CMEMBUS[18]);  // AND_Gate
  and and_21 (and_21_out, or_9_out, CMEMBUS[18]);
  and and_22 (and_22_out, MDR[7], INSTRUCBUS[2]);
  // RSFF rsff_9: pin names not known; wires that end beside it: and_20_out, CLK, and_21_out, rsff_9_p4, PSW[3]
  not not_9 (rsff_9_p4, RST);
  and and_23 (and_23_out, ~and_22_out, CMEMBUS[20]);  // AND_Gate
  and and_24 (and_24_out, and_22_out, CMEMBUS[20]);
  // RSFF rsff_10: pin names not known; wires that end beside it: and_23_out, CLK, and_24_out, rsff_10_p4, PSW[15]
  not not_10 (rsff_10_p4, RST);

  // Other names for the same wires on the sheet: A7__0[7:0] = A[7:0]; A15__0[15:0] = A; A15__8[7:0] = A[15:8];
  //   immed = ADDRBUS[0]; memind = ADDRBUS[1]; regdir = ADDRBUS[2]; regind = ADDRBUS[3]; predec = ADDRBUS[4];
  //   pcrelpom = ADDRBUS[5]; B7__0[7:0] = B[7:0]; B15__8[7:0] = B[15:8]; stFETCH = CFFBUS[0]; clFETCH = CFFBUS[1];
  //   stADDR = CFFBUS[2]; clADDR = CFFBUS[3]; stEXEC = CFFBUS[4]; clEXEC = CFFBUS[5]; stINTR = CFFBUS[6];
  //   clINTR = CFFBUS[7]; ldMAR = CMEMBUS[0]; incMAR = CMEMBUS[1]; ldMDR = CMEMBUS[2]; ldPC = CMEMBUS[3];
  //   incPC = CMEMBUS[4]; mxMAR0 = CMEMBUS[5]; mxMAR1 = CMEMBUS[6]; mxMAR2 = CMEMBUS[7]; mxMDR2 = CMEMBUS[8];
  //   mxMDR1 = CMEMBUS[9]; mxMDR0 = CMEMBUS[10]; decMAR = CMEMBUS[11]; mxPC2 = CMEMBUS[12]; mxPC1 = CMEMBUS[13];
  //   mxPC0 = CMEMBUS[14]; ldSTART = CMEMBUS[15]; ldZ = CMEMBUS[16]; ldN = CMEMBUS[17]; ldV = CMEMBUS[18];
  //   ldC = CMEMBUS[19]; ldI = CMEMBUS[20]; carry = CMEMBUS[21]; clPSWSTART = CPSW[0]; stPSWSTART = CPSW[1];
  //   ldIR31__24 = CREGBUS[0]; ldIR23__16 = CREGBUS[1]; ldIR15__8 = CREGBUS[2]; ldIR7__0 = CREGBUS[3];
  //   ldB15__8 = CREGBUS[4]; ldB7__0 = CREGBUS[5]; mxB0 = CREGBUS[6]; mxB1 = CREGBUS[7]; wrGPR = CREGBUS[8];
  //   mxBDEC = CREGBUS[9]; incSP = CREGBUS[10]; decSP = CREGBUS[11]; mxGRP = CREGBUS[12]; ldDWL = CREGBUS[13];
  //   ldDWH = CREGBUS[14]; Din7__0[7:0] = DIN; DWL[7:0] = DW[7:0]; DWH[7:0] = DW[15:8];
  //   ENTRADDR15__0[15:0] = IVTPPDSP; GPR15__0[7:0] = GPR7__0; GPR15__8[7:0] = GPR15__0; HALT = INSTRUCBUS[0];
  //   RTS = INSTRUCBUS[1]; RTI = INSTRUCBUS[2]; ROR = INSTRUCBUS[3]; PUSH = INSTRUCBUS[4]; POP = INSTRUCBUS[5];
  //   BOVF = INSTRUCBUS[6]; BNCR = INSTRUCBUS[7]; BLEQ = INSTRUCBUS[8]; BLSSU = INSTRUCBUS[9]; JLEQ = INSTRUCBUS[10];
  //   JMP = INSTRUCBUS[11]; JSR = INSTRUCBUS[12]; LD = INSTRUCBUS[13]; ST = INSTRUCBUS[14]; DEC = INSTRUCBUS[15];
  //   SUB = INSTRUCBUS[16]; XOR = INSTRUCBUS[17]; AND = INSTRUCBUS[18]; STRFIND = INSTRUCBUS[19];
  //   IR31__24[3:0] = IR27__24; MAR15__0[15:0] = MAR; MDR7__0[7:0] = MDR; PC15__0[7:0] = PC7__0;
  //   PC15__8[7:0] = PC15__0; FETCH = PHASEFFBUS[0]; ADDR = PHASEFFBUS[1]; EXEC = PHASEFFBUS[2]; INTR = PHASEFFBUS[3];
  //   PSW8b (some bits) = {PSW[15], PSW[4:0]}; PSW15__0[15:0] = PSW; PSWSTART = PSW[0]; PSWZ = PSW[1]; PSWN = PSW[2];
  //   PSWV = PSW[3]; PSWC = PSW[4]; PSWI = PSW[15]

  // Notes on the sheet:
  //   Instrukcijski registar
  //   Pomocni B registrar
  //   Registarski fajl
  //   DW registar
  //   MAR
  //   Dekoderi za prepoznavanje instrukcije na osnovu sadrzaja registra IR31..24
  //   MDR
  //   SP
  //   Dekoder za prepoznavanje nacina adresiranja
  //   Sabirac
  //   FF za pokretanje FETCH, ADDR, EXEC i INTR faze izvršavanja instrukcije
  //   PC
  //   Programska statusna reč (PSW)
endmodule

module FETCH (
  input  in_1,
  input  in_2,
  input  in_3,
  input  [3:0] PHASEFFBUS,
  input  [19:0] INSTRUCBUS,
  input  [5:0] ADDRBUS,
  input  [15:0] PSW,
  output [31:0] CMEMBUS,
  output [7:0] CFFBUS,
  output [14:0] CREGBUS,
  output rdMEM
);

  wire addr2, addr2_t, addr3, addr4, addr_t, and_4_out, and_5_out, and_6_out, and_7_out, and_8_out,
       and_9_out, and_10_out, and_11_out, and_12_out, and_13_out, and_14_out, and_15_out, bezadr1, bezadr1_t,
       braddr2, braddr3, branch2, branch2_t, brbezadr1, brbranch2, brbranch3, brcnd, brgrinst, brjmp3,
       brnotFCBUS, bruncnd, clFETCH, FCBUS_t, grinst, grinst_t, incPC, jmp3, jmp3_t, ldIR7__0, ldIR15__8,
       ldIR23__16, ldIR31__24, ldMAR, ldMDR, not_1_out, not_3_out, not_4_out, notPSWSTandFETCH, or_5_out,
       or_7_out, or_8_out, rdMEM_t, reg8_inc_ld_1_p5, reg8_inc_ld_1_p6, stADDR, stEXEC;
  wire [7:0] reg8_inc_ld_1_p4;
  wire [23:11] rom32x24_1_dout;

  or or_1 (bezadr1, INSTRUCBUS[0], INSTRUCBUS[1], INSTRUCBUS[2], INSTRUCBUS[3], INSTRUCBUS[4], INSTRUCBUS[5]);
  or or_2 (branch2, INSTRUCBUS[6], INSTRUCBUS[7], INSTRUCBUS[8], INSTRUCBUS[9]);
  or or_3 (jmp3, INSTRUCBUS[11], INSTRUCBUS[12]);
  not not_1 (not_1_out, in_1);
  // REG8_INC_LD reg8_inc_ld_1: pin names not known; wires that end beside it: in_2, not_1_out, rom32x24_1_dout[23:16], reg8_inc_ld_1_p4, reg8_inc_ld_1_p5, reg8_inc_ld_1_p6
  or or_4 (reg8_inc_ld_1_p5, bruncnd, brcnd);
  not not_2 (reg8_inc_ld_1_p6, reg8_inc_ld_1_p5);
  ROM32x24 rom32x24_1 (
    .A4__0(reg8_inc_ld_1_p4[4:0]), .CS(1'b1),
    .DOUT({rom32x24_1_dout, stEXEC, stADDR, clFETCH, ldIR7__0, ldIR15__8, ldIR23__16, ldIR31__24, ldMDR, rdMEM_t, incPC, ldMAR}));
  // DC4_16 dc4_16_1: pin names not known; wires that end beside it: rom32x24_1_dout[15:12], 1'b1, bruncnd, notPSWSTandFETCH, brnotFCBUS, brgrinst, brbezadr1, brbranch2, braddr2, brbranch3, brjmp3, braddr3
  or or_5 (or_5_out, ADDRBUS[2], ADDRBUS[3], ADDRBUS[4]);
  or or_6 (addr_t, INSTRUCBUS[13], INSTRUCBUS[14], INSTRUCBUS[15], INSTRUCBUS[16], INSTRUCBUS[17], INSTRUCBUS[18], INSTRUCBUS[19]);
  and and_1 (addr2, addr_t, or_5_out);
  and and_2 (addr3, addr_t, ADDRBUS[5]);
  or or_7 (or_7_out, ADDRBUS[0], ADDRBUS[1]);
  not not_3 (not_3_out, PHASEFFBUS[0]);
  not not_4 (not_4_out, PSW[0]);
  and and_3 (addr4, addr_t, or_7_out);
  or or_8 (or_8_out, not_3_out, not_4_out);
  and and_4 (and_4_out, or_8_out, notPSWSTandFETCH);
  and and_5 (and_5_out, brnotFCBUS, FCBUS_t);
  and and_6 (and_6_out, brgrinst, grinst_t);
  and and_7 (and_7_out, brbezadr1, bezadr1_t);
  and and_8 (and_8_out, brbranch2, branch2_t);
  and and_9 (and_9_out, braddr2, addr2_t);
  and and_10 (and_10_out, brbranch3, INSTRUCBUS[10]);
  and and_11 (and_11_out, brjmp3, jmp3_t);
  and and_12 (and_12_out, braddr3, addr3);
  or or_9 (brcnd, and_4_out, and_5_out, and_6_out, and_7_out, and_8_out, and_9_out, and_10_out, and_11_out, and_12_out);
  and and_13 (and_13_out, ~bezadr1, ~branch2, ~INSTRUCBUS[10], ~jmp3, ~addr_t);  // AND_Gate
  and and_14 (and_14_out, INSTRUCBUS[14], ADDRBUS[0]);
  and and_15 (and_15_out, INSTRUCBUS[15], ADDRBUS[0]);
  or or_10 (grinst, and_13_out, and_14_out, and_15_out);
  assign CFFBUS[1] = clFETCH ? 1'b1 : 1'bz;  // Controlled_Buffer controlled_buffer_1
  assign CMEMBUS[0] = ldMAR ? 1'b1 : 1'bz;  // Controlled_Buffer controlled_buffer_2
  assign CMEMBUS[2] = ldMDR ? 1'b1 : 1'bz;  // Controlled_Buffer controlled_buffer_3
  assign CMEMBUS[4] = incPC ? 1'b1 : 1'bz;  // Controlled_Buffer controlled_buffer_4
  assign CFFBUS[2] = stADDR ? 1'b1 : 1'bz;  // Controlled_Buffer controlled_buffer_5
  assign CFFBUS[4] = stEXEC ? 1'b1 : 1'bz;  // Controlled_Buffer controlled_buffer_6
  assign CREGBUS[0] = ldIR31__24 ? 1'b1 : 1'bz;  // Controlled_Buffer controlled_buffer_7
  assign CREGBUS[1] = ldIR23__16 ? 1'b1 : 1'bz;  // Controlled_Buffer controlled_buffer_8
  assign CREGBUS[2] = ldIR15__8 ? 1'b1 : 1'bz;  // Controlled_Buffer controlled_buffer_9
  assign CREGBUS[3] = ldIR7__0 ? 1'b1 : 1'bz;  // Controlled_Buffer controlled_buffer_10
  assign rdMEM = rdMEM_t ? 1'b1 : 1'bz;  // Controlled_Buffer controlled_buffer_11

  // Other names for the same wires on the sheet: immed = ADDRBUS[0]; memind = ADDRBUS[1]; regdir = ADDRBUS[2];
  //   regind = ADDRBUS[3]; predec = ADDRBUS[4]; pcrelpom = ADDRBUS[5]; CLK = in_2; FCBUS = in_3; HALT = INSTRUCBUS[0];
  //   RTS = INSTRUCBUS[1]; RTI = INSTRUCBUS[2]; ROR = INSTRUCBUS[3]; PUSH = INSTRUCBUS[4]; POP = INSTRUCBUS[5];
  //   BOVF = INSTRUCBUS[6]; BNCR = INSTRUCBUS[7]; BLEQ = INSTRUCBUS[8]; BLSSU = INSTRUCBUS[9];
  //   branch3 = INSTRUCBUS[10]; JLEQ = INSTRUCBUS[10]; JMP = INSTRUCBUS[11]; JSR = INSTRUCBUS[12];
  //   LD = INSTRUCBUS[13]; ST = INSTRUCBUS[14]; DEC = INSTRUCBUS[15]; SUB = INSTRUCBUS[16]; XOR = INSTRUCBUS[17];
  //   AND = INSTRUCBUS[18]; STRFIND = INSTRUCBUS[19]; FETCH = PHASEFFBUS[0]; ADDR = PHASEFFBUS[1];
  //   EXEC = PHASEFFBUS[2]; INTR = PHASEFFBUS[3]; PSWSTART = PSW[0]; rst = in_1

  // Notes on the sheet:
  //   Kontrolna jedinica
  //   Operaciona jedinica
  //   grinst
endmodule

module ADDR (
  input  in_1,
  input  in_2,
  input  in_3,
  input  [3:0] PHASEFFBUS,
  input  [19:0] INSTRUCBUS,
  input  [5:0] ADDRBUS,
  output [31:0] CMEMBUS,
  output [7:0] CFFBUS,
  output [14:0] CREGBUS,
  output rdMEM
);

  wire and_1_out, and_2_out, bradr, brcnd, brnotADDR, brnotFCBUS, bruncnd, bruncnd_t, clADDR, incMAR,
       ldB7__0, ldB15__8, ldMAR, ldMDR, mp2_8b_1_p3, mxB0, mxB1, mxMAR0, mxMAR1, mxMAR2, not_1_out,
       not_3_out, not_4_out, rdMEM_t, reg8_inc_ld_1_p5, reg8_inc_ld_1_p6, stEXEC, wrGPR;
  wire [2:0] dc3_8_1_p1;
  wire [3:0] kmadr_1_out_7;
  wire [6:0] mp2_8b_1_p2;
  wire [7:0] reg8_inc_ld_1_p4;

  KMADR kmadr_1 (
    .immed(ADDRBUS[0]), .memind(ADDRBUS[1]), .regind(ADDRBUS[3]), .regdir(ADDRBUS[2]), .predec(ADDRBUS[4]),
    .pcrelpom(ADDRBUS[5]), .out_7(kmadr_1_out_7));
  not not_1 (not_1_out, in_1);
  // MP2_8b mp2_8b_1: pin names not known; wires that end beside it: bradr, {1'b0, mp2_8b_1_p2}, mp2_8b_1_p3, {4'b0000, kmadr_1_out_7}
  // REG8_INC_LD reg8_inc_ld_1: pin names not known; wires that end beside it: in_2, not_1_out, mp2_8b_1_p3, reg8_inc_ld_1_p4, reg8_inc_ld_1_p5, reg8_inc_ld_1_p6
  not not_2 (reg8_inc_ld_1_p6, reg8_inc_ld_1_p5);
  // DC3_8 dc3_8_1: pin names not known; wires that end beside it: dc3_8_1_p1, 1'b1, bruncnd_t, brnotFCBUS, brnotADDR, bradr
  or or_1 (reg8_inc_ld_1_p5, bruncnd, brcnd, bradr);
  ROM32x24_2 rom32x24_2_1 (
    .A4__0(reg8_inc_ld_1_p4[4:0]), .CS(1'b1),
    .DOUT({mp2_8b_1_p2, dc3_8_1_p1, stEXEC, clADDR, mxMAR2, wrGPR, mxB1, mxMAR1, incMAR, ldMDR, rdMEM_t, mxMAR0, ldMAR, mxB0, ldB7__0, ldB15__8}));
  not not_3 (not_3_out, PHASEFFBUS[1]);
  not not_4 (not_4_out, in_3);
  and and_1 (and_1_out, brnotADDR, not_3_out);
  and and_2 (and_2_out, brnotFCBUS, not_4_out);
  or or_2 (brcnd, and_1_out, and_2_out);
  assign CMEMBUS[0] = ldMAR ? 1'b1 : 1'bz;  // Controlled_Buffer controlled_buffer_1
  assign CMEMBUS[1] = incMAR ? 1'b1 : 1'bz;  // Controlled_Buffer controlled_buffer_2
  assign CMEMBUS[2] = ldMDR ? 1'b1 : 1'bz;  // Controlled_Buffer controlled_buffer_3
  assign CMEMBUS[5] = mxMAR0 ? 1'b1 : 1'bz;  // Controlled_Buffer controlled_buffer_4
  assign CMEMBUS[6] = mxMAR1 ? 1'b1 : 1'bz;  // Controlled_Buffer controlled_buffer_5
  assign CMEMBUS[7] = mxMAR2 ? 1'b1 : 1'bz;  // Controlled_Buffer controlled_buffer_6
  assign CREGBUS[7] = mxB1 ? 1'b1 : 1'bz;  // Controlled_Buffer controlled_buffer_7
  assign CFFBUS[3] = clADDR ? 1'b1 : 1'bz;  // Controlled_Buffer controlled_buffer_8
  assign CFFBUS[4] = stEXEC ? 1'b1 : 1'bz;  // Controlled_Buffer controlled_buffer_9
  assign CREGBUS[4] = ldB15__8 ? 1'b1 : 1'bz;  // Controlled_Buffer controlled_buffer_10
  assign CREGBUS[5] = ldB7__0 ? 1'b1 : 1'bz;  // Controlled_Buffer controlled_buffer_11
  assign CREGBUS[6] = mxB0 ? 1'b1 : 1'bz;  // Controlled_Buffer controlled_buffer_12
  assign CREGBUS[8] = wrGPR ? 1'b1 : 1'bz;  // Controlled_Buffer controlled_buffer_13
  assign rdMEM = rdMEM_t ? 1'b1 : 1'bz;  // Controlled_Buffer controlled_buffer_14

  // Other names for the same wires on the sheet: immed = ADDRBUS[0]; memind = ADDRBUS[1]; regdir = ADDRBUS[2];
  //   regind = ADDRBUS[3]; predec = ADDRBUS[4]; pcrelpom = ADDRBUS[5]; CLK = in_2; FCBUS = in_3; ADDR = PHASEFFBUS[1];
  //   rst = in_1

  // Notes on the sheet:
  //   Operaciona jedinica
  //   Upravljacka jedinica
endmodule

module EXEC (
  input  in_1,
  input  in_2,
  input  in_3,
  input  [15:0] B,
  input  [3:0] PHASEFFBUS,
  input  [19:0] INSTRUCBUS,
  input  [5:0] ADDRBUS,
  input  [15:0] PSW,
  input  [7:0] in_9,
  output [15:0] A,
  output [15:0] ALU,
  output [31:0] CMEMBUS,
  output [7:0] CFFBUS,
  output [14:0] CREGBUS,
  output [5:0] CPSW,
  output rdMEM,
  output wrMEM
);

  wire and_1_out, and_2_out, and_3_out, and_4_out, and_5_out, and_6_out, and_7_out, and_8_out, and_9_out,
       brcnd, brnotbrorjmp, brnotbrorjmp_t, brnotEXEC, brnotEXEC_t, brnotFCBUS, brnotFOUNDINDEX,
       brnotFOUNDINDEX_t, bropr, brorjmp, brregdir, bruncnd, carry, clEXEC, clindeks, clPSWSTART, decMAR,
       decSP, FOUNDINDEX, incindeks, incMAR, incSP, ldA7__0, ldA15__8, ldB7__0, ldB15__8, ldC, ldDWH, ldDWL,
       ldI, ldMAR, ldMDR, ldN, ldPC, ldSTART, ldV, ldZ, mp2_8b_1_p3, mp4_8b_1_p5, mp4_8b_2_p5, mxA0, mxA1,
       mxB0, mxB1, mxBDEC, mxGPR, mxMAR0, mxMAR1, mxMAR2, mxMDR0, mxMDR1, mxMDR2, mxPC0, mxPC1, mxPC2,
       not_1_out, not_2_out, not_3_out, or_2_out, or_3_out, rdMEM_t, reg8_inc_ld_1_p5, reg8_inc_ld_1_p6, srA,
       stINTR, undriven, undriven_2, undriven_3, undriven_4, wrGPR, wrMEM_t, xor_1_out;
  wire [2:0] rom128x56_1_dout;
  wire [6:0] kmadr_exec_1_out_21;
  wire [7:0] reg8_inc_ld_1_p4;
  wire [15:0] indeks;
  wire [31:22] dc3_8_1_p1;

  // DC3_8 dc3_8_1: pin names not known; wires that end beside it: dc3_8_1_p1[24:22], 1'b1, bruncnd, brnotEXEC, brregdir, brnotFCBUS, brnotbrorjmp_t, brnotFOUNDINDEX, bropr
  // MP4_8b mp4_8b_1: pin names not known; wires that end beside it: mxA1, mxA0, B[15:8], indeks[15:8], mp4_8b_1_p5, ALU[15:8], in_9, 1'b1
  not not_1 (not_1_out, in_1);
  // REG8_LD_SL_SR reg8_ld_sl_sr_1: pin names not known; wires that end beside it: A[0], srA, in_2, not_1_out, mp4_8b_1_p5, A[15:8], ldA15__8
  KMADR_EXEC kmadr_exec_1 (
    .LD(INSTRUCBUS[13]), .ST(INSTRUCBUS[14]), .DEC(INSTRUCBUS[15]), .SUB(INSTRUCBUS[16]),
    .XOR(INSTRUCBUS[17]), .AND(INSTRUCBUS[18]), .STRFIND(INSTRUCBUS[19]), .BOVF(INSTRUCBUS[6]),
    .BNCR(INSTRUCBUS[7]), .BLEQ(INSTRUCBUS[8]), .BLSSU(INSTRUCBUS[9]), .JLEQ(INSTRUCBUS[10]),
    .JMP(INSTRUCBUS[11]), .JSR(INSTRUCBUS[12]), .RTS(INSTRUCBUS[1]), .RTI(INSTRUCBUS[2]),
    .ROR(INSTRUCBUS[3]), .PUSH(INSTRUCBUS[4]), .POP(INSTRUCBUS[5]), .HALT(INSTRUCBUS[0]),
    .out_21(kmadr_exec_1_out_21));
  not not_2 (not_2_out, in_1);
  not not_3 (not_3_out, in_1);
  // MP4_8b mp4_8b_2: pin names not known; wires that end beside it: mxA1, mxA0, B[7:0], indeks[7:0], mp4_8b_2_p5, ALU[7:0], in_9, 1'b1
  // REG8_LD_SL_SR reg8_ld_sl_sr_2: pin names not known; wires that end beside it: A[8], srA, in_2, not_2_out, mp4_8b_2_p5, A[7:0], ldA7__0
  // MP2_8b mp2_8b_1: pin names not known; wires that end beside it: bropr, {1'b0, dc3_8_1_p1[31:25]}, mp2_8b_1_p3, {1'b0, kmadr_exec_1_out_21}, 1'b1
  // REG8_INC_LD reg8_inc_ld_1: pin names not known; wires that end beside it: in_2, not_3_out, mp2_8b_1_p3, reg8_inc_ld_1_p4, reg8_inc_ld_1_p5, reg8_inc_ld_1_p6
  not not_4 (reg8_inc_ld_1_p6, reg8_inc_ld_1_p5);
  ROM128x56 rom128x56_1 (
    .A6__0(reg8_inc_ld_1_p4[6:0]), .CS(1'b1),
    .DOUT_2({dc3_8_1_p1, clEXEC, stINTR, clPSWSTART, srA, mxPC0, ldDWH, ldDWL, decSP, mxMAR0, incSP, mxPC1, mxPC2, ldPC, incindeks, mxA0, clindeks, mxMAR1, mxA1, decMAR, wrMEM_t, mxMDR2, mxB1}),
    .DOUT({mxB0, mxBDEC, ldB7__0, ldB15__8, mxGPR, wrGPR, mxMDR1, mxMAR2, incMAR, mxMDR0, ldMDR, ldSTART, ldI, ldC, ldV, ldZ, ldN, ldA7__0, ldA15__8, ldMAR, rdMEM_t, rom128x56_1_dout}));
  or or_1 (reg8_inc_ld_1_p5, bruncnd, brcnd, bropr);
  // REG16 reg16_1: pin names not known; wires that end beside it: clindeks, in_2, indeks, incindeks
  Comparator comparator_1 (.a(A[7:0]), .b(in_9), .eq(FOUNDINDEX));  // open: gt, lt
  ALU16_SUB_XOR_AND alu16_sub_xor_and_1 (
    .Cin(1'b0), .A(A), .B(B), .sub(INSTRUCBUS[16]), .\xor (INSTRUCBUS[17]), .\and (INSTRUCBUS[18]), .F(ALU),
    .Cout(carry));
  and and_1 (and_1_out, PSW[3], INSTRUCBUS[6]);
  and and_2 (and_2_out, ~PSW[4], INSTRUCBUS[7]);  // AND_Gate
  xor xor_1 (xor_1_out, PSW[2], PSW[3]);
  and and_3 (and_3_out, PSW[4], INSTRUCBUS[9]);
  and and_4 (and_4_out, ~PHASEFFBUS[2], brnotEXEC_t);  // AND_Gate
  and and_5 (and_5_out, ADDRBUS[2], brregdir);
  and and_6 (and_6_out, ~in_3, brnotFCBUS);  // AND_Gate
  and and_7 (and_7_out, brorjmp, brnotbrorjmp);
  and and_8 (and_8_out, ~FOUNDINDEX, brnotFOUNDINDEX_t);  // AND_Gate
  or or_2 (or_2_out, xor_1_out, PSW[1]);
  or or_3 (or_3_out, INSTRUCBUS[8], INSTRUCBUS[10]);
  and and_9 (and_9_out, or_2_out, or_3_out);
  or or_4 (brorjmp, and_1_out, and_2_out, and_9_out, and_3_out);
  or or_5 (brcnd, and_4_out, and_5_out, and_6_out, and_7_out, and_8_out);
  assign CMEMBUS[0] = ldMAR ? 1'b1 : 1'bz;  // Controlled_Buffer controlled_buffer_1
  assign CMEMBUS[14] = mxPC0 ? 1'b1 : 1'bz;  // Controlled_Buffer controlled_buffer_2
  assign CMEMBUS[18] = ldV ? 1'b1 : 1'bz;  // Controlled_Buffer controlled_buffer_3
  assign CMEMBUS[1] = incMAR ? 1'b1 : 1'bz;  // Controlled_Buffer controlled_buffer_4
  assign CMEMBUS[6] = mxMAR1 ? 1'b1 : 1'bz;  // Controlled_Buffer controlled_buffer_5
  assign CMEMBUS[10] = mxMDR0 ? 1'b1 : 1'bz;  // Controlled_Buffer controlled_buffer_6
  assign CMEMBUS[19] = ldC ? 1'b1 : 1'bz;  // Controlled_Buffer controlled_buffer_7
  Controlled_Buffer controlled_buffer_8 (.in(1'b1), .en(undriven));  // open: out
  assign CREGBUS[6] = mxB0 ? 1'b1 : 1'bz;  // Controlled_Buffer controlled_buffer_9
  assign CREGBUS[7] = mxB1 ? 1'b1 : 1'bz;  // Controlled_Buffer controlled_buffer_10
  assign CMEMBUS[2] = ldMDR ? 1'b1 : 1'bz;  // Controlled_Buffer controlled_buffer_11
  assign CMEMBUS[7] = mxMAR2 ? 1'b1 : 1'bz;  // Controlled_Buffer controlled_buffer_12
  assign CMEMBUS[11] = decMAR ? 1'b1 : 1'bz;  // Controlled_Buffer controlled_buffer_13
  assign CMEMBUS[15] = ldSTART ? 1'b1 : 1'bz;  // Controlled_Buffer controlled_buffer_14
  assign CMEMBUS[20] = ldI ? 1'b1 : 1'bz;  // Controlled_Buffer controlled_buffer_15
  Controlled_Buffer controlled_buffer_16 (.in(1'b1), .en(undriven_2));  // open: out
  assign CREGBUS[5] = ldB7__0 ? 1'b1 : 1'bz;  // Controlled_Buffer controlled_buffer_17
  assign CREGBUS[8] = wrGPR ? 1'b1 : 1'bz;  // Controlled_Buffer controlled_buffer_18
  assign CMEMBUS[3] = ldPC ? 1'b1 : 1'bz;  // Controlled_Buffer controlled_buffer_19
  assign CMEMBUS[8] = mxMDR2 ? 1'b1 : 1'bz;  // Controlled_Buffer controlled_buffer_20
  assign CMEMBUS[12] = mxPC2 ? 1'b1 : 1'bz;  // Controlled_Buffer controlled_buffer_21
  assign CMEMBUS[16] = ldZ ? 1'b1 : 1'bz;  // Controlled_Buffer controlled_buffer_22
  assign CMEMBUS[21] = carry ? 1'b1 : 1'bz;  // Controlled_Buffer controlled_buffer_23
  Controlled_Buffer controlled_buffer_24 (.in(1'b1), .en(undriven_3));  // open: out
  assign CREGBUS[9] = mxBDEC ? 1'b1 : 1'bz;  // Controlled_Buffer controlled_buffer_25
  assign CMEMBUS[5] = mxMAR0 ? 1'b1 : 1'bz;  // Controlled_Buffer controlled_buffer_26
  assign CMEMBUS[9] = mxMDR1 ? 1'b1 : 1'bz;  // Controlled_Buffer controlled_buffer_27
  assign CMEMBUS[13] = mxPC1 ? 1'b1 : 1'bz;  // Controlled_Buffer controlled_buffer_28
  assign CMEMBUS[17] = ldN ? 1'b1 : 1'bz;  // Controlled_Buffer controlled_buffer_29
  Controlled_Buffer controlled_buffer_30 (.in(1'b1), .en(undriven_4));  // open: out
  assign CREGBUS[4] = ldB15__8 ? 1'b1 : 1'bz;  // Controlled_Buffer controlled_buffer_31
  assign CREGBUS[10] = incSP ? 1'b1 : 1'bz;  // Controlled_Buffer controlled_buffer_32
  assign CREGBUS[12] = mxGPR ? 1'b1 : 1'bz;  // Controlled_Buffer controlled_buffer_33
  assign CFFBUS[5] = clEXEC ? 1'b1 : 1'bz;  // Controlled_Buffer controlled_buffer_34
  assign CREGBUS[11] = decSP ? 1'b1 : 1'bz;  // Controlled_Buffer controlled_buffer_35
  assign CREGBUS[13] = ldDWL ? 1'b1 : 1'bz;  // Controlled_Buffer controlled_buffer_36
  assign CFFBUS[6] = stINTR ? 1'b1 : 1'bz;  // Controlled_Buffer controlled_buffer_37
  assign CREGBUS[14] = ldDWH ? 1'b1 : 1'bz;  // Controlled_Buffer controlled_buffer_38
  assign CPSW[0] = clPSWSTART ? 1'b1 : 1'bz;  // Controlled_Buffer controlled_buffer_39
  assign rdMEM = rdMEM_t ? 1'b1 : 1'bz;  // Controlled_Buffer controlled_buffer_40
  assign wrMEM = wrMEM_t ? 1'b1 : 1'bz;  // Controlled_Buffer controlled_buffer_41

  // Other names for the same wires on the sheet: A7__0[7:0] = A[7:0]; A15__0[15:0] = A; A15__8[7:0] = A[15:8];
  //   regdir = ADDRBUS[2]; ALU7__0[7:0] = ALU[7:0]; ALU15__8[7:0] = ALU[15:8]; B7__0[7:0] = B[7:0]; B15__0[15:0] = B;
  //   B15__8[7:0] = B[15:8]; CLK = in_2; FCBUS = in_3; indeks7__0[7:0] = indeks[7:0]; indeks15__8[7:0] = indeks[15:8];
  //   HALT = INSTRUCBUS[0]; RTS = INSTRUCBUS[1]; RTI = INSTRUCBUS[2]; ROR = INSTRUCBUS[3]; PUSH = INSTRUCBUS[4];
  //   POP = INSTRUCBUS[5]; BOVF = INSTRUCBUS[6]; BNCR = INSTRUCBUS[7]; BLEQ = INSTRUCBUS[8]; BLSSU = INSTRUCBUS[9];
  //   JLEQ = INSTRUCBUS[10]; JMP = INSTRUCBUS[11]; JSR = INSTRUCBUS[12]; LD = INSTRUCBUS[13]; ST = INSTRUCBUS[14];
  //   DEC = INSTRUCBUS[15]; SUB = INSTRUCBUS[16]; XOR = INSTRUCBUS[17]; AND = INSTRUCBUS[18];
  //   STRFIND = INSTRUCBUS[19]; MDR[7:0] = in_9; EXEC = PHASEFFBUS[2]; PSWSTART = PSW[0]; PSWZ = PSW[1];
  //   PSWN = PSW[2]; PSWV = PSW[3]; PSWC = PSW[4]; PSWI = PSW[15]; rst = in_1

  // Notes on the sheet:
  //   MDR
  //   Operaciona jedinica
  //   Upravljacka jedinica
endmodule

module INTR (
  input  in_1,
  input  in_2,
  input  in_3,
  input  [3:0] PHASEFFBUS,
  input  [19:0] INSTRUCBUS,
  input  [15:0] PSW,
  input  [7:0] intr,
  output [15:0] ADDIVTP,
  output [2:0] UEXT2__0,
  output inta,
  output [31:0] CMEMBUS,
  output [7:0] CFFBUS,
  output [14:0] CREGBUS,
  output rdMEM,
  output wrMEM
);

  wire and_2_out, and_3_out, and_4_out, brcnd, brnotFCBUS, brnotINTR, brnotprekid, bruncnd, clINTR, incMAR,
       incSP, ldDWH, ldDWL, ldMAR, ldMDR, ldPC, mxMAR0, mxMAR1, mxMAR2, mxMDR0, mxMDR1, mxMDR2, mxPC0, mxPC1,
       not_1_out, not_2_out, not_3_out, prekid, prper, rdMEM_t, reg8_inc_ld_1_p5, reg8_inc_ld_1_p6, stFETCH,
       wrMEM_t;
  wire [2:0] dc3_8_1_p1;
  wire [3:0] rom32x32_1_dout;
  wire [3:1] IVTDSP15__0;
  wire [4:0] reg8_inc_ld_1_p3;
  wire [7:0] reg8_inc_ld_1_p4;
  wire [15:0] IVTP15__0;

  and and_1 (prekid, prper, PSW[15], not_1_out);
  // DC3_8 dc3_8_1: pin names not known; wires that end beside it: dc3_8_1_p1, 1'b1, bruncnd, brnotINTR, brnotprekid, brnotFCBUS
  not not_1 (not_1_out, INSTRUCBUS[0]);
  not not_2 (not_2_out, in_1);
  // REG16_LD reg16_ld_1: pin names not known; wires that end beside it: in_2, not_2_out, IVTP15__0
  not not_3 (not_3_out, in_1);
  // REG8_INC_LD reg8_inc_ld_1: pin names not known; wires that end beside it: in_2, not_3_out, {3'b000, reg8_inc_ld_1_p3}, reg8_inc_ld_1_p4, reg8_inc_ld_1_p5, reg8_inc_ld_1_p6
  or or_1 (reg8_inc_ld_1_p5, bruncnd, brcnd);
  not not_4 (reg8_inc_ld_1_p6, reg8_inc_ld_1_p5);
  ROM32x32 rom32x32_1 (
    .A4__0(reg8_inc_ld_1_p4[4:0]), .CS(1'b1),
    .DOUT({reg8_inc_ld_1_p3, dc3_8_1_p1, clINTR, stFETCH, mxPC1, mxPC0, ldPC, ldDWH, ldDWL, incMAR, rdMEM_t, wrMEM_t, inta, incSP, mxMDR2, mxMDR1, mxMDR0, ldMDR, mxMAR2, mxMAR1, mxMAR0, ldMAR, rom32x32_1_dout}));
  or or_2 (prper, intr[7], intr[6], intr[5], intr[4], intr[3], intr[2], intr[1], intr[0]);
  // CD8 cd8_1: pin names not known; wires that end beside it: intr[7], intr[6], intr[5], intr[4], intr[3], intr[2], intr[1], intr[0], 1'b1, UEXT2__0[2], UEXT2__0[1], UEXT2__0[0]
  and and_2 (and_2_out, ~PHASEFFBUS[3], brnotINTR);  // AND_Gate
  and and_3 (and_3_out, ~prekid, brnotprekid);  // AND_Gate
  and and_4 (and_4_out, ~in_3, brnotFCBUS);  // AND_Gate
  or or_3 (brcnd, and_2_out, and_3_out, and_4_out);
  // REG3_LD reg3_ld_1: pin names not known; wires that end beside it: in_2, UEXT2__0, IVTDSP15__0, inta
  // ADD16 add16_1: pin names not known; wires that end beside it: IVTP15__0, ADDIVTP, {{12{1'b0}}, IVTDSP15__0, 1'b0}, 1'b0
  assign CMEMBUS[0] = ldMAR ? 1'b1 : 1'bz;  // Controlled_Buffer controlled_buffer_1
  assign CMEMBUS[2] = ldMDR ? 1'b1 : 1'bz;  // Controlled_Buffer controlled_buffer_2
  assign CMEMBUS[10] = mxMDR0 ? 1'b1 : 1'bz;  // Controlled_Buffer controlled_buffer_3
  assign CMEMBUS[3] = ldPC ? 1'b1 : 1'bz;  // Controlled_Buffer controlled_buffer_4
  assign CREGBUS[10] = incSP ? 1'b1 : 1'bz;  // Controlled_Buffer controlled_buffer_5
  assign CMEMBUS[5] = mxMAR0 ? 1'b1 : 1'bz;  // Controlled_Buffer controlled_buffer_6
  assign CMEMBUS[8] = mxMDR2 ? 1'b1 : 1'bz;  // Controlled_Buffer controlled_buffer_7
  assign CMEMBUS[13] = mxPC1 ? 1'b1 : 1'bz;  // Controlled_Buffer controlled_buffer_8
  assign CMEMBUS[1] = incMAR ? 1'b1 : 1'bz;  // Controlled_Buffer controlled_buffer_9
  assign CMEMBUS[6] = mxMAR1 ? 1'b1 : 1'bz;  // Controlled_Buffer controlled_buffer_10
  assign CMEMBUS[9] = mxMDR1 ? 1'b1 : 1'bz;  // Controlled_Buffer controlled_buffer_11
  assign CMEMBUS[14] = mxPC0 ? 1'b1 : 1'bz;  // Controlled_Buffer controlled_buffer_12
  assign CREGBUS[13] = ldDWL ? 1'b1 : 1'bz;  // Controlled_Buffer controlled_buffer_13
  assign CMEMBUS[7] = mxMAR2 ? 1'b1 : 1'bz;  // Controlled_Buffer controlled_buffer_14
  assign CFFBUS[0] = stFETCH ? 1'b1 : 1'bz;  // Controlled_Buffer controlled_buffer_15
  assign CFFBUS[7] = clINTR ? 1'b1 : 1'bz;  // Controlled_Buffer controlled_buffer_16
  assign CREGBUS[14] = ldDWH ? 1'b1 : 1'bz;  // Controlled_Buffer controlled_buffer_17
  assign rdMEM = rdMEM_t ? 1'b1 : 1'bz;  // Controlled_Buffer controlled_buffer_18
  assign wrMEM = wrMEM_t ? 1'b1 : 1'bz;  // Controlled_Buffer controlled_buffer_19

  // Other names for the same wires on the sheet: ldBR = inta; ADDIVTP15__0[15:0] = ADDIVTP; CLK = in_2; FCBUS = in_3;
  //   HALT = INSTRUCBUS[0]; intr7__0[7:0] = intr; INTR_t = PHASEFFBUS[3]; PSWI = PSW[15]; rst = in_1

  // Notes on the sheet:
  //   Operaciona jedinica
  //   Upravljacka jedinica
endmodule

module RAM (
  input  [15:0] in_1,
  input  in_2,
  input  [7:0] in_3,
  input  in_4,
  input  in_5,
  input  in_6,
  output [7:0] out_7,
  output out_8
);

  wire and_1_out, and_2_out, CNT0, LDCNT, not_1_out, notCNT0, or_1_out, reg4_ld_sl_sr_1_p6, rsff_2_p4,
       rsff_2_p5, rsff_3_p4, sl;
  wire [3:0] CNT, LFSR;

  // RSFF rsff_1: pin names not known; wires that end beside it: 1'b0, in_2, in_6, sl
  or or_1 (or_1_out, in_4, in_5);
  // REG4_LD_SL_SR reg4_ld_sl_sr_1: pin names not known; wires that end beside it: 1'b0, 1'b0, in_2, 4'b1111, LFSR, reg4_ld_sl_sr_1_p6, sl, in_6
  // RisingEdge risingedge_1: pin names not known; wires that end beside it: or_1_out, in_2, LDCNT
  // MEM64Kx8 mem64kx8_1: pin names not known; wires that end beside it: in_1, 1'b1, in_2, in_3, out_7, in_4
  xor xor_1 (reg4_ld_sl_sr_1_p6, LFSR[2], LFSR[3]);
  and and_1 (and_1_out, CNT0, not_1_out);
  not not_1 (not_1_out, LDCNT);
  // RSFF rsff_2: pin names not known; wires that end beside it: and_1_out, in_2, LDCNT, rsff_2_p4, rsff_2_p5
  not not_2 (rsff_2_p4, in_6);
  and and_2 (and_2_out, rsff_2_p5, CNT0);
  // REG4m_DEC_LD reg4m_dec_ld_1: pin names not known; wires that end beside it: in_2, LFSR, CNT, LDCNT, notCNT0, notCNT0
  or or_2 (notCNT0, CNT[0], CNT[1], CNT[2], CNT[3]);
  // RSFF rsff_3: pin names not known; wires that end beside it: out_8, in_2, and_2_out, rsff_3_p4, out_8
  not not_3 (rsff_3_p4, in_6);
  not not_4 (CNT0, notCNT0);

  // Other names for the same wires on the sheet: ADR[15:0] = in_1; CLK = in_2; DIN[7:0] = in_3; DOUT[7:0] = out_7;
  //   fc = out_8; RDMEM = in_5; rst = in_6; WRMEM = in_4

  // Notes on the sheet:
  //   Random broj predstavlja vreme pristupa memoriji
  //   Brojac za generisanje random broja 
  //   Jedinica za generisanje function complete (fc) signala
  //   Brojac za dekrementiranje random broja
endmodule
